# Fritzing sketch ROX-2X modified (saved by Fritzing 0.9.3b)

parts:
  RE1 = Rotary Encoder [package=THT]
  LCD1 = LCD screen
  Mod1 = Raspberry Pi Pico
  Part1 = Adafruit Si5351A Clock Generator [part_number="Adafruit #2045"]
  S1 = Pushbutton [package="[THT]"]
  S2 = Pushbutton [package="[THT]"]
  S3 = Pushbutton [package="[THT]"]
  S4 = Pushbutton [package="[THT]"]
  R2 = Resistor [tolerance=±5% resistance=3.3k package="2010 [SMD]"]
  R3 = Resistor [tolerance=±5% resistance=240k package="0402 [SMD]"]
  LED1 = LED - 5mm [color="Green (570nm)" package="5 mm [THT]"]
  D3 = Schottky Diode [part_number=1N5817 package="300 mil [THT]"]
  R4 = Resistor [tolerance=±5% resistance=3.3k package="2010 [SMD]"]
  R5 = TRIMPOT [package=trimpot-3mm]
  LED2 = LED - 5mm [color="Red (633nm)" package="5 mm [THT]"]
  L1 = Inductor [package="400 mil [THT]"]
  C1 = Ceramic Capacitor [capacitance=43nF package="100 mil [THT, multilayer]"]
  R6 = Resistor [tolerance=±5% resistance=50 package=THT]
  D4 = Schottky Diode [part_number=1N5817 package="300 mil [THT]"]
  D5 = Schottky Diode [part_number=1N5817 package="300 mil [THT]"]
  R7 = Resistor [tolerance=±5% resistance=91k package="0402 [SMD]"]
  R1 = Rotary Potentiometer (Small) [maximum_resistance=47kΩ package=THT]
  R8 = Resistor [tolerance=±5% resistance=330 package="2010 [SMD]"]
  C2 = Ceramic Capacitor [capacitance=43nF package="100 mil [THT, multilayer]"]
  L2 = Inductor [package="400 mil [THT]"]
  C3 = Ceramic Capacitor [capacitance=43nF package="100 mil [THT, multilayer]"]
  C4 = Ceramic Capacitor [capacitance=43nF package="100 mil [THT, multilayer]"]
  C5 = Ceramic Capacitor [capacitance=43nF package="100 mil [THT, multilayer]"]
  C6 = Ceramic Capacitor [capacitance=43nF package="100 mil [THT, multilayer]"]
  R9 = Resistor [tolerance=±5% resistance=220 package="2010 [SMD]"]
  R10 = Resistor [tolerance=±5% resistance=220 package="2010 [SMD]"]
  R11 = Resistor [tolerance=±5% resistance=56 package=THT]
  R12 = Resistor [tolerance=±5% resistance=56 package=THT]
  S5 = Pushbutton [package="[THT]"]
  J1 = female pin header, 1 pin [form="♀ (female)"]
  J2 = female pin header, 1 pin [form="♀ (female)"]
  J3 = female pin header, 1 pin [form="♀ (female)"]
  J4 = female pin header, 1 pin [form="♀ (female)"]
  J5 = female pin header, 1 pin [form="♀ (female)"]
  J6 = female pin header, 1 pin [form="♀ (female)"]
  J7 = female pin header, 1 pin [form="♀ (female)"]
  J8 = female pin header, 1 pin [form="♀ (female)"]
  J9 = female pin header, 1 pin [form="♀ (female)"]

nets:
  N1: RE1.EncoderPinA, Mod1.pin_20
  GND: RE1.EncoderPinC, LCD1.VSS, LCD1.R/W, Mod1.pin_3, Mod1.pin_8, Mod1.pin_13, Mod1.pin_18, Mod1.pin_23, Mod1.pin_28, Mod1.pin_33, Mod1.pin_38, Mod1.pin_42, Part1.GND, S1.Pin_1, S1.Pin_2, S2.Pin_1, S2.Pin_2, S3.Pin_1, S3.Pin_2, S4.Pin_1, S4.Pin_2, R5.CCW, C1.0, R6.Pin_0, R7.Pin_1, R1.leg1, R1.wiper, C2.0, C3.0, R11.Pin_1, R12.Pin_1, S5.Pin_1, S5.Pin_2
  N2: RE1.EncoderPinB, Mod1.pin_19
  VDD: LCD1.VDD, Mod1.pin_39, Part1.VIN, D3.cathode, R5.WIPER
  N3: LCD1.V0, R5.CW
  N4: LCD1.RS, Mod1.pin_21
  N5: LCD1.E, Mod1.pin_22
  N6: LCD1.DB4, Mod1.pin_24
  N7: LCD1.DB5, Mod1.pin_25
  N8: LCD1.DB6, Mod1.pin_26
  N9: LCD1.DB7, Mod1.pin_27
  N10: Mod1.pin_6, Part1.SDA, R4.Pin_1
  N11: Mod1.pin_7, Part1.SCL, R2.Pin_1
  N12: Mod1.pin_14, S3.Pin_3, S3.Pin_4
  N13: Mod1.pin_15, S1.Pin_3, S1.Pin_4
  N14: Mod1.pin_16, S2.Pin_3, S2.Pin_4
  N15: Mod1.pin_17, S4.Pin_3, S4.Pin_4
  N16: Mod1.pin_30, S5.Pin_4
  N17: Mod1.pin_31, D4.anode, J3.pin1
  N18: Mod1.pin_32, R3.Pin_1, D5.anode, R7.Pin_0
  N19: Mod1.pin_36, R2.Pin_0, R4.Pin_0, D4.cathode, D5.cathode
  N20: Part1.CLK0, C4.0
  N21: Part1.CLK1, C5.0
  N22: Part1.CLK2, C6.0
  N23: R3.Pin_0, LED1.anode, J4.pin1
  N24: LED1.cathode, J2.pin1
  N25: D3.anode, LED2.anode, J6.pin1
  N26: LED2.cathode, J5.pin1
  N27: L1.pin_0, C2.1, L2.pin_1
  N28: L1.pin_1, C1.1, R6.Pin_1, R8.Pin_0
  N29: R1.leg2, J1.pin1
  N30: R8.Pin_1, C4.1
  N31: L2.pin_0, C3.1, J7.pin1
  N32: C5.1, R9.Pin_1
  N33: C6.1, R10.Pin_1
  N34: R9.Pin_0, R12.Pin_0, J8.pin1
  N35: R10.Pin_0, R11.Pin_0, J9.pin1

notes:
  +4V5
  +3V3
  +5V
  GND
  +9VBATT
  RSSI
  Q1_COL
  LED1
  240kΩ
  91kΩ
  To R14
  D5
  RF_GAIN
  RV2.2
  Encoder
  330Ω
  50Ω
  43p
  60p
  56n
  LO to SA636
  1n
  220Ω
  56Ω
  Signal injection
  SA636 RF input
  Schottky
  I2C
  Reset
  Contrast
  3.3kΩ

custom parts:
  Raspberry Pi Pico: Raspberry Pi Pico. Based around the RP2040 microcontroller the Pico is a low cost microcontroller device bringing Raspberry Pi quality, cost, and easy of use to the microcontroller space. Jan 2021, Split part in to two versions: tht (this one) and SMD. This one will drill holes for a .1 in header in pcb to allow plugging in the module as well as providing pads to solder the module to the top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
  Adafruit Si5351A Clock Generator: Never hunt around for another crystal again, with the Si5351A clock generator breakout from Adafruit! This chip has a precision 25MHz crystal reference and internal PLL and dividers so it can generate just about any frequency, from <8KHz up to 150+ MHz. The Si5351A clock generator is an I2C controller clock generator. It uses the onboard precision clock to drive multiple PLL's and clock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
